# Fritzing sketch potentiometer-a0 (saved by Fritzing 0.9.3b)
breadboards: 1

parts:
  U1 = NodeMCU V1.0
  U2 = POT [package=pot_mammoth]
  VCC1 = 4 x AAA Battery Mount

nets:
  N1: U1.3V3, U2.E
  N2: U1.GND, U2.A, VCC1.-
  N3: U1.Vin, VCC1.+
  N4: U1.A0, U2.S

custom parts:
  NodeMCU V1.0: ESP8266 based NodeMCU
